# Fritzing sketch Timer_Display (saved by Fritzing 0.7.1b)
breadboards: 1

parts:
  U1 = Arduino Mega
  Contrast = Rotary Potentiometer (Small) [maximum_resistance=200]
  Time_Setup = Rotary Potentiometer (Small) [maximum_resistance=100kΩ]
  J1 = Piezo Speaker
  Alarm_Led = LED - 5mm [color="Red (633nm)" package="5 mm [THT]"]
  R3 = Resistor [tolerance=±5% resistance=220 package=THT]
  R4 = Resistor [tolerance=±5% resistance=220 package=THT]
  Reset_Time = Pushbutton [package=THT]
  Mute_Speeker = Pushbutton [package=THT]
  R5 = Resistor [tolerance=±5% resistance=220 package=THT]
  R6 = Resistor [tolerance=±5% resistance=220 package=THT]
  R7 = Resistor [tolerance=±5% resistance=220 package=THT]
  GLCD = female pin header, 20 pins [form="♀ (female)"]

nets:
  N1: U1.RST, GLCD.pin4
  N2: U1.A0, Time_Setup.wiper
  N3: U1.D22, GLCD.pin14
  N4: U1.D23, GLCD.pin13
  N5: U1.D24, GLCD.pin12
  N6: U1.D25, GLCD.pin11
  N7: U1.D26, GLCD.pin10
  N8: U1.D27, GLCD.pin9
  N9: U1.D28, GLCD.pin8
  N10: U1.D29, GLCD.pin7
  N11: U1.D33, GLCD.pin6
  N12: U1.D34, GLCD.pin5
  N13: U1.D35, GLCD.pin16
  N14: U1.D36, GLCD.pin17
  N15: U1.D37, GLCD.pin15
  N16: U1.D40, R4.Pin_0, Reset_Time.leg0
  N17: U1.D41, Mute_Speeker.leg0, R5.Pin_0
  N18: U1.D42, Alarm_Led.anode
  N19: U1.D43, J1.pin2
  N20: Contrast.leg1, GLCD.pin1, GLCD.pin19
  N21: Contrast.wiper, GLCD.pin18
  N22: Contrast.leg2, GLCD.pin3
  N23: Time_Setup.leg1, Reset_Time.leg1, Mute_Speeker.leg1
  N24: Time_Setup.leg2, R4.Pin_1, R5.Pin_1, R6.Pin_1, R7.Pin_1
  N25: J1.pin1, R7.Pin_0
  N26: Alarm_Led.cathode, R6.Pin_0
  N27: R3.Pin_0, GLCD.pin2
